// Logisim project COA_EXPO_PROJECT_SIGNAL_STRENGTH.circ as structural Verilog: 12 circuits, main circuit main
module main (
  input  [7:0] in_1,
  input  [7:0] in_2,
  input  [7:0] in_3,
  input  [7:0] in_4,
  output [24:0] out_5,
  output [7:0] out_6,
  output [4:0] out_7,
  output [7:0] out_8,
  output [7:0] out_9,
  output [7:0] out_10,
  output [7:0] out_11,
  output [7:0] out_12,
  output [7:0] out_13
);

  wire ALU_Save, C_Save, Carry_Flag, clk, INPort_R, not_1_out, not_2_out, not_3_out, OUTPort_W, Reg_R, Reg_W,
       SRAM_R, SRAM_W, Stack_R, Stack_W, T0, T1, T2, T3, T4, UpdatePC, Z_Save, Zero_Flag;
  wire [3:0] x, y, z;
  wire [4:0] _1_out, _2_out, _3_out, _4_out, _5_out;
  wire [7:0] ALUOut, Dout_INPort, Dout_SRAM, Dout_Stack, Imm, multiplexer_1_out, multiplexer_2_out,
       multiplexer_4_out, multiplexer_5_out, multiplexer_6_out, PC_D2, Rx, Ry;

  Multiplexer #(.select(5), .width(8), .enable("false")) multiplexer_1 (
    .in13(Imm), .in14(Imm), .in15(Imm), .in16(Imm), .in17(Imm), .in27(ALUOut), .in28(ALUOut),
    .out(multiplexer_1_out), .sel(out_7));  // open: in0, in1, in2, in3, in4, in5, in6, in7, in8, in9, in10, in11, in12, in18, in19, in20, in21, in22, in23, in24, in25, in26, in29, in30, in31
  PC pc_1 (
    .EnablePC(T0), .clk(clk), .UpdatePC(UpdatePC), .NewCAddress(multiplexer_1_out), .PC(out_6), .PC_D2(PC_D2));  // open: PC_D1
  Clock clock_1 (.out(clk));
  OUTPort outport_1 (
    .DatainOUTPort(ALUOut), .clk(clk), .W(OUTPort_W), .CurrentAddress(Imm),
    .DatavisibletoExternal1World(out_8), .DatavisibletoExternal2World(out_9),
    .DatavisibletoExternal3World(out_10), .DatavisibletoExternal4World(out_11),
    .DatavisibletoExternal5World(out_12), .DatavisibletoExternal6World(out_13));
  ROM_SynR rom_synr_1 (
    .Address(out_6), .clk(clk), .R(T0), .Inst(out_5), .Imm(Imm), .Source2(y), .Source1(x), .Dest(z),
    .OPCODE(out_7));  // open: Imm_D1, Source2_D1, Source1_D1, Dest_D1, OPCODE_D1, Inst_D1, Inst_D2, Inst_D3, Imm_D2, Source2_D2, Source1_D2, Dest_D2, OPCODE_D2, Imm_D3, Source2_D3, Source1_D3, Dest_D3, OPCODE_D3
  Timing timing_1 (.clk(clk), .T0(T0), .T1(T1), .T2(T2), .T3(T3), .T4(T4));
  INPort inport_1 (
    .DatacomingfromExternal1World(in_1), .clk(clk), .R(INPort_R), .DatacomingfromExternal2World(in_2),
    .DatacomingfromExternal3World(in_3), .DatacomingfromExternal4World(in_4), .CurrentAddress(Imm),
    .INPortDataout(Dout_INPort));  // open: INPort1Dout, INPort2Dout, INPort3Dout, INPort4Dout
  assign _1_out = out_8[4:0] & out_13[4:0];  // AND_Gate _1, 5 bits wide
  assign _2_out = out_9[4:0] & out_13[4:0];  // AND_Gate _2, 5 bits wide
  DotMatrix #(.matrixrows(5)) dotmatrix_1 (.col0(_1_out), .col1(_2_out), .col2(_3_out), .col3(_4_out), .col4(_5_out));
  assign _3_out = out_10[4:0] & out_13[4:0];  // AND_Gate _3, 5 bits wide
  assign _4_out = out_11[4:0] & out_13[4:0];  // AND_Gate _4, 5 bits wide
  Stack stack_1 (.Din(ALUOut), .W(Stack_W), .clk(clk), .R(Stack_R), .Dout(Dout_Stack));  // open: SPWritePTR, SPReadPTR
  Multiplexer #(.select(5), .width(8), .enable("false")) multiplexer_2 (
    .in1(ALUOut), .in2(ALUOut), .in3(ALUOut), .in4(ALUOut), .in5(ALUOut), .in6(ALUOut), .in7(ALUOut),
    .in8(ALUOut), .in9(ALUOut), .in10(ALUOut), .in11(Dout_SRAM), .in19(Dout_Stack), .in20(Dout_INPort),
    .in22(Dout_SRAM), .in24(ALUOut), .in25(ALUOut), .in26(ALUOut), .out(multiplexer_2_out), .sel(out_7));  // open: in0, in12, in13, in14, in15, in16, in17, in18, in21, in23, in27, in28, in29, in30, in31
  assign _5_out = out_12[4:0] & out_13[4:0];  // AND_Gate _5, 5 bits wide
  not not_1 (not_1_out, Carry_Flag);
  not not_2 (not_2_out, Zero_Flag);
  Register_File register_file_1 (
    .clk(clk), .Datain(multiplexer_2_out), .AddressW(z), .W(Reg_W), .R(Reg_R), .AddressR1(x), .AddressR2(y),
    .Rx(Rx), .Ry(Ry));
  not not_3 (not_3_out, Zero_Flag);
  Multiplexer #(.select(5), .disabled(0)) multiplexer_3 (
    .in0(1'b0), .in1(1'b0), .in2(1'b0), .in3(1'b0), .in4(1'b0), .in5(1'b0), .in6(1'b0), .in7(1'b0),
    .in8(1'b0), .in9(1'b0), .in10(1'b0), .in11(1'b0), .in12(1'b0), .in13(1'b1), .in14(Zero_Flag),
    .in15(not_3_out), .in16(Carry_Flag), .in17(not_1_out), .in18(1'b0), .in19(1'b0), .in20(1'b0),
    .in21(1'b0), .in22(1'b0), .in23(1'b0), .in24(1'b0), .in25(1'b0), .in26(1'b0), .in27(Zero_Flag),
    .in28(not_2_out), .in29(1'b0), .in30(1'b0), .in31(1'b0), .out(UpdatePC), .sel(out_7), .en(T4));
  Multiplexer #(.select(5), .width(8), .enable("false")) multiplexer_4 (
    .in0({8{1'b0}}), .in1(Rx), .in2(Rx), .in3(Rx), .in4(Rx), .in5(Rx), .in6(Rx), .in7(Rx), .in8(Rx),
    .in9(Rx), .in10({8{1'b0}}), .in11({8{1'b0}}), .in12(Rx), .in13({8{1'b0}}), .in14({8{1'b0}}),
    .in15({8{1'b0}}), .in16({8{1'b0}}), .in17({8{1'b0}}), .in18(Rx), .in19({8{1'b0}}), .in20({8{1'b0}}),
    .in21(Rx), .in22({8{1'b0}}), .in23({8{1'b0}}), .in24(Rx), .in25(Rx), .in26(Rx), .in27(PC_D2),
    .in28(PC_D2), .in29({8{1'b0}}), .in30({8{1'b0}}), .in31({8{1'b0}}), .out(multiplexer_4_out), .sel(out_7));
  Multiplexer #(.select(5), .width(8), .enable("false")) multiplexer_5 (
    .in11(Imm), .in12(Imm), .in22(Rx), .in23(Rx), .out(multiplexer_5_out), .sel(out_7));  // open: in0, in1, in2, in3, in4, in5, in6, in7, in8, in9, in10, in13, in14, in15, in16, in17, in18, in19, in20, in21, in24, in25, in26, in27, in28, in29, in30, in31
  Multiplexer #(.select(5), .width(8), .enable("false")) multiplexer_6 (
    .in0({8{1'b0}}), .in1(Ry), .in2(Ry), .in3(Ry), .in4(Ry), .in5(Imm), .in6(Imm), .in7(Imm), .in8(Imm),
    .in9({8{1'b0}}), .in10(Imm), .in11({8{1'b0}}), .in12({8{1'b0}}), .in13({8{1'b0}}), .in14({8{1'b0}}),
    .in15({8{1'b0}}), .in16({8{1'b0}}), .in17({8{1'b0}}), .in18({8{1'b0}}), .in19({8{1'b0}}),
    .in20({8{1'b0}}), .in21({8{1'b0}}), .in22({8{1'b0}}), .in23(Ry), .in24(Ry), .in25(Ry), .in26(Ry),
    .in27({1'b0, Imm[6:0]}), .in28({1'b0, Imm[6:0]}), .in29({8{1'b0}}), .in30({8{1'b0}}), .in31({8{1'b0}}),
    .out(multiplexer_6_out), .sel(out_7));
  MUX32to1_1bit mux32to1_1bit_1 (.Inp32bit(32'h801000), .Sel(out_7), .E(T3), .Out(SRAM_W));
  MUX32to1_1bit mux32to1_1bit_2 (.Inp32bit(32'h400800), .Sel(out_7), .E(T3), .Out(SRAM_R));
  MUX32to1_1bit mux32to1_1bit_3 (.Inp32bit(32'h7e413fe), .Sel(out_7), .E(T1), .Out(Reg_R));
  MUX32to1_1bit mux32to1_1bit_4 (.Inp32bit(32'h7580ffe), .Sel(out_7), .E(T4), .Out(Reg_W));
  MUX32to1_1bit mux32to1_1bit_5 (.Inp32bit(32'h200000), .Sel(out_7), .E(T3), .Out(OUTPort_W));
  MUX32to1_1bit mux32to1_1bit_6 (.Inp32bit(32'h100000), .Sel(out_7), .E(T3), .Out(INPort_R));
  ALU alu_1 (
    .Operand1(multiplexer_4_out), .Operand2(multiplexer_6_out), .CFlag_Save(C_Save), .clk(clk),
    .ALUOut(ALUOut), .CarryFlag(Carry_Flag), .ZeroFlag(Zero_Flag), .ALU_Save(ALU_Save), .OPCODE(out_7),
    .ZFlag_Save(Z_Save), .Imm7(Imm[7]));  // open: ALUOut_D1
  DataMemorySRAM datamemorysram_1 (
    .Address(multiplexer_5_out), .Din(ALUOut), .W(SRAM_W), .clk(clk), .R(SRAM_R), .Dout(Dout_SRAM));
  MUX32to1_1bit mux32to1_1bit_7 (.Inp32bit(32'h1fa417fe), .Sel(out_7), .E(T2), .Out(ALU_Save));
  MUX32to1_1bit mux32to1_1bit_8 (.Inp32bit(32'h70001fe), .Sel(out_7), .E(T2), .Out(Z_Save));
  MUX32to1_1bit mux32to1_1bit_9 (.Inp32bit(32'h7000110), .Sel(out_7), .E(T2), .Out(C_Save));
  MUX32to1_1bit mux32to1_1bit_10 (.Inp32bit(32'h40000), .Sel(out_7), .E(T3), .Out(Stack_W));
  MUX32to1_1bit mux32to1_1bit_11 (.Inp32bit(32'h80000), .Sel(out_7), .E(T3), .Out(Stack_R));

  // Other names for the same wires on the sheet: OPCODE[4:0] = out_7
endmodule

module DataMemorySRAM (
  input  [7:0] Address,
  input  [7:0] Din,
  input  W,
  input  clk,
  input  R,
  output [7:0] Dout
);

  wire [7:0] ram_1_data;

  RAM #(.bus("separate")) ram_1 (
    .addr(Address), .din(Din), .data(ram_1_data), .str(W), .sel(1'b1), .clk(clk), .ld(1'b1), .clr(1'b0));
  Register register_1 (.D(ram_1_data), .en(R), .Q(Dout), .clk(clk), .clr(1'b0));
endmodule

module Stack (
  input  [7:0] Din,
  input  W,
  input  clk,
  input  R,
  output [7:0] Dout,
  output [7:0] SPWritePTR,
  output [7:0] SPReadPTR
);

  wire or_1_out;
  wire [7:0] adder_1_out, multiplexer_1_out, multiplexer_2_out;

  Adder adder_1 (.a(SPWritePTR), .b(8'h1), .out(adder_1_out), .cin(1'b0));  // open: cout
  Subtractor subtractor_1 (.a(SPWritePTR), .b(8'h1), .out(SPReadPTR), .bin(1'b0));  // open: bout
  Multiplexer #(.select(2), .width(8), .disabled(0), .enable("false")) multiplexer_1 (
    .in0(SPWritePTR), .in1(adder_1_out), .in2(SPReadPTR), .out(multiplexer_1_out), .sel({R, W}));  // open: in3
  or or_1 (or_1_out, W, R);
  DataMemorySRAM datamemorysram_1 (.Address(multiplexer_2_out), .Din(Din), .W(W), .clk(clk), .R(R), .Dout(Dout));
  Register register_1 (.D(multiplexer_1_out), .en(or_1_out), .Q(SPWritePTR), .clk(clk), .clr(1'b0));
  Multiplexer #(.select(2), .width(8), .disabled(0), .enable("false")) multiplexer_2 (
    .in0({8{1'b0}}), .in1(SPWritePTR), .in2(SPReadPTR), .out(multiplexer_2_out), .sel({R, W}));  // open: in3
endmodule

module RegisterSynR (
  input  [7:0] Din,
  input  W,
  input  clk,
  input  R,
  output [7:0] Dout
);

  wire [7:0] register_1_q;

  Register register_1 (.D(Din), .en(W), .Q(register_1_q), .clk(clk), .clr(1'b0));
  Register register_2 (.D(register_1_q), .en(R), .Q(Dout), .clk(clk), .clr(1'b0));
endmodule

module ROM_SynR (
  input  [7:0] Address,
  input  clk,
  input  R,
  output [24:0] Inst,
  output [24:0] Inst_D1,
  output [24:0] Inst_D2,
  output [24:0] Inst_D3,
  output [7:0] Imm,
  output [3:0] Source2,
  output [7:0] Imm_D1,
  output [7:0] Imm_D2,
  output [7:0] Imm_D3,
  output [3:0] Source1,
  output [3:0] Dest,
  output [3:0] Source2_D1,
  output [3:0] Source2_D2,
  output [3:0] Source2_D3,
  output [4:0] OPCODE,
  output [3:0] Source1_D1,
  output [3:0] Source1_D2,
  output [3:0] Source1_D3,
  output [3:0] Dest_D1,
  output [3:0] Dest_D2,
  output [3:0] Dest_D3,
  output [4:0] OPCODE_D1,
  output [4:0] OPCODE_D2,
  output [4:0] OPCODE_D3
);

  wire [24:0] rom_1_data;

  ROM #(.dataWidth(25)) rom_1 (.addr(Address), .data(rom_1_data), .sel(1'b1));
  Register #(.width(25)) register_1 (
    .D(rom_1_data), .en(R), .Q({Inst[24:20], Dest, Inst[15:8], Imm}), .clk(clk), .clr(1'b0));
  Register #(.width(25)) register_2 (
    .D({Inst[24:20], Dest, Inst[15:8], Imm}), .en(1'b1),
    .Q({Inst_D1[24:20], Dest_D1, Inst_D1[15:8], Imm_D1}), .clk(clk), .clr(1'b0));
  Register #(.width(25)) register_3 (
    .D({Inst_D1[24:20], Dest_D1, Inst_D1[15:8], Imm_D1}), .en(1'b1),
    .Q({Inst_D2[24:20], Dest_D2, Inst_D2[15:8], Imm_D2}), .clk(clk), .clr(1'b0));
  Register #(.width(25)) register_4 (
    .D({Inst_D2[24:20], Dest_D2, Inst_D2[15:8], Imm_D2}), .en(1'b1),
    .Q({Inst_D3[24:20], Dest_D3, Inst_D3[15:8], Imm_D3}), .clk(clk), .clr(1'b0));

  assign {Inst[19:16], Inst[7:0]} = {Dest, Imm};
  assign {Inst_D1[19:16], Inst_D1[7:0]} = {Dest_D1, Imm_D1};
  assign {Inst_D2[19:16], Inst_D2[7:0]} = {Dest_D2, Imm_D2};
  assign {Inst_D3[19:16], Inst_D3[7:0]} = {Dest_D3, Imm_D3};
  assign OPCODE = Inst[24:20];
  assign OPCODE_D1 = Inst_D1[24:20];
  assign OPCODE_D2 = Inst_D2[24:20];
  assign OPCODE_D3 = Inst_D3[24:20];
  assign Source1 = Inst[15:12];
  assign Source1_D1 = Inst_D1[15:12];
  assign Source1_D2 = Inst_D2[15:12];
  assign Source1_D3 = Inst_D3[15:12];
  assign Source2 = Inst[11:8];
  assign Source2_D1 = Inst_D1[11:8];
  assign Source2_D2 = Inst_D2[11:8];
  assign Source2_D3 = Inst_D3[11:8];

  // Notes on the sheet:
  //   contents of rom_1 (hex, n*v repeats v):
  //   aa0050 ab003c ac0028 ad0014 ae0000 14000f1 d00010 9*0 1810a00 1100020 a50001 a60003 a70007 a8000f
  //   a9001f 15050f8 15060f9 15070fa 15080fb 15090fc d000b0 0 0 0 1810b00 1100030 a50001 a60003 a70007
  //   a8000f a90000 15050f8 15060f9 15070fa 15080fb 15090fc d000b0 0 0 0 1810c00 1100040 a50001 a60003
  //   a70007 a80000 a90000 15050f8 15060f9 15070fa 15080fb 15090fc d000b0 0 0 0 1810d00 1100050 a50001
  //   a60003 a70000 a80000 a90000 15050f8 15060f9 15070fa 15080fb 15090fc d000b0 0 0 0 1810e00 1100060
  //   e00060 a50001 a60000 a70000 a80000 a90000 15050f8 15060f9 15070fa 15080fb 15090fc d000b0 0 0 a40000
  //   15040fd a50000 a60000 a70004 a80000 a90000 15050f8 15060f9 15070fa 15080fb 15090fc a400ff 15040fd
  //   d00070 0 a40000 15040fd a50000 a60000 a70000 a80000 a90000 15090f8 15080f9 15070fa 15060fb 15050fc
  //   a400ff 15040fd d00080 0 a40000 15040fd a50000 a6000e a7000a a8000e a90000 15050f8 15060f9 15070fa
  //   15080fb 15090fc a400ff 15040fd d00090 0 a40000 15040fd a50000 a60000 a70000 a80000 a90000 15090f8
  //   15080f9 15070fa 15060fb 15050fc a400ff 15040fd d000a0 0 a40000 15040fd a5001f a60011 a70011 a80011
  //   a9001f 15050f8 15060f9 15070fa 15080fb 15090fc a400ff 15040fd d000b0 0 a40000 15040fd a50000 a60000
  //   a70000 a80000 a90000 15090f8 15080f9 15070fa 15060fb 15050fc a400ff 15040fd d00005 0 d00005
endmodule

module ALU (
  input  Imm7,
  input  [7:0] Operand1,
  input  [7:0] Operand2,
  input  [4:0] OPCODE,
  input  ALU_Save,
  input  CFlag_Save,
  input  ZFlag_Save,
  input  clk,
  output [7:0] ALUOut,
  output [7:0] ALUOut_D1,
  output CarryFlag,
  output ZeroFlag
);

  wire Cout, multiplexer_3_out, nor_1_out;
  wire [7:0] ANDAnswer, ExORAnswer, LShiftAnswer, multiplexer_2_out, ORAnswer, RShiftAnswer, SUM, xor_1_out;
  wire [7:7] multiplexer_1_out;

  assign xor_1_out = {8{multiplexer_1_out[7]}} ^ Operand2;  // XOR_Gate xor_1, 8 bits wide
  Multiplexer #(.select(5), .enable("false")) multiplexer_1 (
    .in0(1'b0), .in1(1'b0), .in2(1'b0), .in3(1'b0), .in4(1'b0), .in5(1'b0), .in6(1'b0), .in7(1'b0),
    .in8(1'b0), .in9(1'b0), .in10(1'b0), .in11(1'b0), .in12(1'b0), .in13(1'b0), .in14(1'b0), .in15(1'b0),
    .in16(1'b0), .in17(1'b0), .in18(1'b0), .in19(1'b0), .in20(1'b0), .in21(1'b0), .in22(1'b0), .in23(1'b0),
    .in24(1'b1), .in25(1'b0), .in26(1'b0), .in27(Imm7), .in28(Imm7), .in29(1'b0), .in30(1'b0), .in31(1'b0),
    .out(multiplexer_1_out[7]), .sel(OPCODE));
  Adder adder_1 (.a(Operand1), .b(xor_1_out), .out(SUM), .cin(multiplexer_1_out[7]), .cout(Cout));
  assign ANDAnswer = Operand1 & Operand2;  // AND_Gate and_1, 8 bits wide
  assign ORAnswer = Operand1 | Operand2;  // OR_Gate or_1, 8 bits wide
  assign ExORAnswer = Operand1 ^ Operand2;  // XOR_Gate xor_2, 8 bits wide
  Shifter shifter_1 (.in(Operand1), .\dist (Operand2[2:0]), .out(LShiftAnswer));
  Shifter #(.shift("lr")) shifter_2 (.in(Operand1), .\dist (Operand2[2:0]), .out(RShiftAnswer));
  Multiplexer #(.select(5), .width(8), .enable("false")) multiplexer_2 (
    .in0(SUM), .in1(ANDAnswer), .in2(ORAnswer), .in3(ExORAnswer), .in4(SUM), .in5(ANDAnswer), .in6(ORAnswer),
    .in7(ExORAnswer), .in8(SUM), .in9(SUM), .in10(SUM), .in11({8{1'b0}}), .in12(SUM), .in13({8{1'b0}}),
    .in14({8{1'b0}}), .in15({8{1'b0}}), .in16({8{1'b0}}), .in17({8{1'b0}}), .in18(SUM), .in19({8{1'b0}}),
    .in20({8{1'b0}}), .in21(SUM), .in22({8{1'b0}}), .in23(SUM), .in24(SUM), .in25(RShiftAnswer),
    .in26(LShiftAnswer), .in27(SUM), .in28(SUM), .in29({8{1'b0}}), .in30({8{1'b0}}), .in31({8{1'b0}}),
    .out(multiplexer_2_out), .sel(OPCODE));
  Multiplexer #(.select(5), .enable("false")) multiplexer_3 (
    .in0(1'b0), .in1(1'b0), .in2(1'b0), .in3(1'b0), .in4(Cout), .in5(1'b0), .in6(1'b0), .in7(1'b0),
    .in8(Cout), .in9(1'b0), .in10(1'b0), .in11(1'b0), .in12(1'b0), .in13(1'b0), .in14(1'b0), .in15(1'b0),
    .in16(1'b0), .in17(1'b0), .in18(1'b0), .in19(1'b0), .in20(1'b0), .in21(1'b0), .in22(1'b0), .in23(1'b0),
    .in24(Cout), .in25(Operand1[0]), .in26(Operand1[7]), .in27(1'b0), .in28(1'b0), .in29(1'b0), .in30(1'b0),
    .in31(1'b0), .out(multiplexer_3_out), .sel(OPCODE));
  nor nor_1 (nor_1_out, multiplexer_2_out[0], multiplexer_2_out[1], multiplexer_2_out[2], multiplexer_2_out[3], multiplexer_2_out[4], multiplexer_2_out[5], multiplexer_2_out[6], multiplexer_2_out[7]);
  Register register_1 (.D(multiplexer_2_out), .en(ALU_Save), .Q(ALUOut), .clk(clk), .clr(1'b0));
  Register #(.width(1)) register_2 (.D(multiplexer_3_out), .en(CFlag_Save), .Q(CarryFlag), .clk(clk), .clr(1'b0));
  Register #(.width(1)) register_3 (.D(nor_1_out), .en(ZFlag_Save), .Q(ZeroFlag), .clk(clk), .clr(1'b0));
  Register register_4 (.D(ALUOut), .en(1'b1), .Q(ALUOut_D1), .clk(clk), .clr(1'b0));

  // Other names for the same wires on the sheet: Rx0 = Operand1[0]; Rx7 = Operand1[7]

  // Notes on the sheet:
  //   This is M (which controls Adder/Subtractor)
endmodule

module Timing (
  input  clk,
  output T0,
  output T1,
  output T2,
  output T3,
  output T4
);

  wire [2:0] adder_1_out, multiplexer_1_out, register_1_q;

  Adder #(.width(3)) adder_1 (.a(register_1_q), .b(3'b001), .out(adder_1_out), .cin(1'b0));  // open: cout
  Multiplexer #(.width(3), .enable("false")) multiplexer_1 (
    .in0(adder_1_out), .in1(3'b000), .out(multiplexer_1_out), .sel(T4));
  Register #(.width(3)) register_1 (.D(multiplexer_1_out), .en(1'b1), .Q(register_1_q), .clk(clk), .clr(1'b0));
  Decoder #(.select(3), .enable("false")) decoder_1 (
    .out0(T0), .out1(T1), .out2(T2), .out3(T3), .out4(T4), .sel(register_1_q));  // open: out5, out6, out7
endmodule

module PC (
  input  EnablePC,
  input  clk,
  input  [7:0] NewCAddress,
  input  UpdatePC,
  output [7:0] PC,
  output [7:0] PC_D1,
  output [7:0] PC_D2
);

  wire [7:0] adder_1_out, multiplexer_1_out, multiplexer_2_out;

  Multiplexer #(.width(8), .enable("false")) multiplexer_1 (
    .in0({8{1'b0}}), .in1(8'h1), .out(multiplexer_1_out), .sel(EnablePC));
  Adder adder_1 (.a(PC), .b(multiplexer_1_out), .out(adder_1_out), .cin(1'b0));  // open: cout
  Multiplexer #(.width(8), .enable("false")) multiplexer_2 (
    .in0(adder_1_out), .in1(NewCAddress), .out(multiplexer_2_out), .sel(UpdatePC));
  Register register_1 (.D(multiplexer_2_out), .en(1'b1), .Q(PC), .clk(clk), .clr(1'b0));
  Register register_2 (.D(PC), .en(1'b1), .Q(PC_D1), .clk(clk), .clr(1'b0));
  Register register_3 (.D(PC_D1), .en(1'b1), .Q(PC_D2), .clk(clk), .clr(1'b0));
endmodule

module Register_File (
  input  clk,
  input  [7:0] Datain,
  input  [3:0] AddressR1,
  input  [3:0] AddressW,
  input  W,
  input  [3:0] AddressR2,
  input  R,
  output [7:0] Rx,
  output [7:0] Ry
);

  wire decoder_1_out0, decoder_1_out1, decoder_1_out2, decoder_1_out3, decoder_1_out4, decoder_1_out5,
       decoder_1_out6, decoder_1_out7, decoder_1_out8, decoder_1_out9, decoder_1_out10, decoder_1_out11,
       decoder_1_out12, decoder_1_out13, decoder_1_out14, decoder_1_out15;
  wire [7:0] D0, D1, D2, D3, D4, D5, D6, D7, D8, D9, D10, D11, D12, D13, D14, D15;

  Decoder #(.select(4), .disabled(0)) decoder_1 (
    .out0(decoder_1_out0), .out1(decoder_1_out1), .out2(decoder_1_out2), .out3(decoder_1_out3),
    .out4(decoder_1_out4), .out5(decoder_1_out5), .out6(decoder_1_out6), .out7(decoder_1_out7),
    .out8(decoder_1_out8), .out9(decoder_1_out9), .out10(decoder_1_out10), .out11(decoder_1_out11),
    .out12(decoder_1_out12), .out13(decoder_1_out13), .out14(decoder_1_out14), .out15(decoder_1_out15),
    .sel(AddressW), .en(W));
  RegisterSynR registersynr_1 (.Din(Datain), .W(decoder_1_out0), .clk(clk), .R(R), .Dout(D0));
  RegisterSynR registersynr_2 (.Din(Datain), .W(decoder_1_out1), .clk(clk), .R(R), .Dout(D1));
  RegisterSynR registersynr_3 (.Din(Datain), .W(decoder_1_out2), .clk(clk), .R(R), .Dout(D2));
  RegisterSynR registersynr_4 (.Din(Datain), .W(decoder_1_out3), .clk(clk), .R(R), .Dout(D3));
  RegisterSynR registersynr_5 (.Din(Datain), .W(decoder_1_out4), .clk(clk), .R(R), .Dout(D4));
  RegisterSynR registersynr_6 (.Din(Datain), .W(decoder_1_out5), .clk(clk), .R(R), .Dout(D5));
  RegisterSynR registersynr_7 (.Din(Datain), .W(decoder_1_out6), .clk(clk), .R(R), .Dout(D6));
  RegisterSynR registersynr_8 (.Din(Datain), .W(decoder_1_out7), .clk(clk), .R(R), .Dout(D7));
  RegisterSynR registersynr_9 (.Din(Datain), .W(decoder_1_out8), .clk(clk), .R(R), .Dout(D8));
  RegisterSynR registersynr_10 (.Din(Datain), .W(decoder_1_out9), .clk(clk), .R(R), .Dout(D9));
  RegisterSynR registersynr_11 (.Din(Datain), .W(decoder_1_out10), .clk(clk), .R(R), .Dout(D10));
  RegisterSynR registersynr_12 (.Din(Datain), .W(decoder_1_out11), .clk(clk), .R(R), .Dout(D11));
  RegisterSynR registersynr_13 (.Din(Datain), .W(decoder_1_out12), .clk(clk), .R(R), .Dout(D12));
  RegisterSynR registersynr_14 (.Din(Datain), .W(decoder_1_out13), .clk(clk), .R(R), .Dout(D13));
  RegisterSynR registersynr_15 (.Din(Datain), .W(decoder_1_out14), .clk(clk), .R(R), .Dout(D14));
  RegisterSynR registersynr_16 (.Din(Datain), .W(decoder_1_out15), .clk(clk), .R(R), .Dout(D15));
  Multiplexer #(.select(4), .width(8), .enable("false")) multiplexer_1 (
    .in0(D0), .in1(D1), .in2(D2), .in3(D3), .in4(D4), .in5(D5), .in6(D6), .in7(D7), .in8(D8), .in9(D9),
    .in10(D10), .in11(D11), .in12(D12), .in13(D13), .in14(D14), .in15(D15), .out(Rx), .sel(AddressR1));
  Multiplexer #(.select(4), .width(8), .enable("false")) multiplexer_2 (
    .in0(D0), .in1(D1), .in2(D2), .in3(D3), .in4(D4), .in5(D5), .in6(D6), .in7(D7), .in8(D8), .in9(D9),
    .in10(D10), .in11(D11), .in12(D12), .in13(D13), .in14(D14), .in15(D15), .out(Ry), .sel(AddressR2));
endmodule

module INPort (
  input  [7:0] DatacomingfromExternal1World,
  input  clk,
  input  R,
  input  [7:0] DatacomingfromExternal2World,
  input  [7:0] DatacomingfromExternal3World,
  input  [7:0] DatacomingfromExternal4World,
  input  [7:0] CurrentAddress,
  output [7:0] INPort1Dout,
  output [7:0] INPortDataout,
  output [7:0] INPort2Dout,
  output [7:0] INPort3Dout,
  output [7:0] INPort4Dout
);

  wire comparator_1_eq, comparator_2_eq, comparator_3_eq, comparator_4_eq;
  wire [1:0] priority_encoder_1_out;

  Comparator #(.mode("unsigned")) comparator_1 (.a(CurrentAddress), .b(8'hf1), .eq(comparator_1_eq));  // open: gt, lt
  Comparator #(.mode("unsigned")) comparator_2 (.a(CurrentAddress), .b(8'hf2), .eq(comparator_2_eq));  // open: gt, lt
  Comparator #(.mode("unsigned")) comparator_3 (.a(CurrentAddress), .b(8'hf3), .eq(comparator_3_eq));  // open: gt, lt
  Comparator #(.mode("unsigned")) comparator_4 (.a(CurrentAddress), .b(8'hf4), .eq(comparator_4_eq));  // open: gt, lt
  RegisterSynR registersynr_1 (.Din(DatacomingfromExternal1World), .W(1'b1), .clk(clk), .R(R), .Dout(INPort1Dout));
  RegisterSynR registersynr_2 (.Din(DatacomingfromExternal2World), .W(1'b1), .clk(clk), .R(R), .Dout(INPort2Dout));
  RegisterSynR registersynr_3 (.Din(DatacomingfromExternal3World), .W(1'b1), .clk(clk), .R(R), .Dout(INPort3Dout));
  RegisterSynR registersynr_4 (.Din(DatacomingfromExternal4World), .W(1'b1), .clk(clk), .R(R), .Dout(INPort4Dout));
  Priority_Encoder #(.select(2)) priority_encoder_1 (
    .in0(comparator_1_eq), .in1(comparator_2_eq), .in2(comparator_3_eq), .in3(comparator_4_eq),
    .out(priority_encoder_1_out), .en_in(1'b1));  // open: gs, en_out
  Multiplexer #(.select(2), .width(8), .enable("false")) multiplexer_1 (
    .in0(INPort1Dout), .in1(INPort2Dout), .in2(INPort3Dout), .in3(INPort4Dout), .out(INPortDataout),
    .sel(priority_encoder_1_out));
endmodule

module OUTPort (
  input  [7:0] DatainOUTPort,
  input  clk,
  input  W,
  input  [7:0] CurrentAddress,
  output [7:0] DatavisibletoExternal1World,
  output [7:0] DatavisibletoExternal2World,
  output [7:0] DatavisibletoExternal3World,
  output [7:0] DatavisibletoExternal4World,
  output [7:0] DatavisibletoExternal5World,
  output [7:0] DatavisibletoExternal6World
);

  wire and_1_out, and_2_out, and_3_out, and_4_out, and_5_out, and_6_out, comparator_1_eq, comparator_2_eq,
       comparator_3_eq, comparator_4_eq, comparator_5_eq, comparator_6_eq;

  Comparator #(.mode("unsigned")) comparator_1 (.a(CurrentAddress), .b(8'hf8), .eq(comparator_1_eq));  // open: gt, lt
  Comparator #(.mode("unsigned")) comparator_2 (.a(CurrentAddress), .b(8'hf9), .eq(comparator_2_eq));  // open: gt, lt
  Comparator #(.mode("unsigned")) comparator_3 (.a(CurrentAddress), .b(8'hfa), .eq(comparator_3_eq));  // open: gt, lt
  Comparator #(.mode("unsigned")) comparator_4 (.a(CurrentAddress), .b(8'hfb), .eq(comparator_4_eq));  // open: gt, lt
  Comparator #(.mode("unsigned")) comparator_5 (.a(CurrentAddress), .b(8'hfc), .eq(comparator_5_eq));  // open: gt, lt
  Comparator #(.mode("unsigned")) comparator_6 (.a(CurrentAddress), .b(8'hfd), .eq(comparator_6_eq));  // open: gt, lt
  and and_1 (and_1_out, W, comparator_1_eq);
  and and_2 (and_2_out, W, comparator_2_eq);
  and and_3 (and_3_out, W, comparator_3_eq);
  and and_4 (and_4_out, W, comparator_4_eq);
  and and_5 (and_5_out, W, comparator_5_eq);
  and and_6 (and_6_out, W, comparator_6_eq);
  Register register_1 (.D(DatainOUTPort), .en(and_1_out), .Q(DatavisibletoExternal1World), .clk(clk), .clr(1'b0));
  Register register_2 (.D(DatainOUTPort), .en(and_2_out), .Q(DatavisibletoExternal2World), .clk(clk), .clr(1'b0));
  Register register_3 (.D(DatainOUTPort), .en(and_3_out), .Q(DatavisibletoExternal3World), .clk(clk), .clr(1'b0));
  Register register_4 (.D(DatainOUTPort), .en(and_4_out), .Q(DatavisibletoExternal4World), .clk(clk), .clr(1'b0));
  Register register_5 (.D(DatainOUTPort), .en(and_5_out), .Q(DatavisibletoExternal5World), .clk(clk), .clr(1'b0));
  Register register_6 (.D(DatainOUTPort), .en(and_6_out), .Q(DatavisibletoExternal6World), .clk(clk), .clr(1'b0));
endmodule

module MUX32to1_1bit (
  input  [31:0] Inp32bit,
  input  [4:0] Sel,
  input  E,
  output Out
);

  Multiplexer #(.select(5), .disabled(0)) multiplexer_1 (
    .in0(Inp32bit[0]), .in1(Inp32bit[1]), .in2(Inp32bit[2]), .in3(Inp32bit[3]), .in4(Inp32bit[4]),
    .in5(Inp32bit[5]), .in6(Inp32bit[6]), .in7(Inp32bit[7]), .in8(Inp32bit[8]), .in9(Inp32bit[9]),
    .in10(Inp32bit[10]), .in11(Inp32bit[11]), .in12(Inp32bit[12]), .in13(Inp32bit[13]), .in14(Inp32bit[14]),
    .in15(Inp32bit[15]), .in16(Inp32bit[16]), .in17(Inp32bit[17]), .in18(Inp32bit[18]), .in19(Inp32bit[19]),
    .in20(Inp32bit[20]), .in21(Inp32bit[21]), .in22(Inp32bit[22]), .in23(Inp32bit[23]), .in24(Inp32bit[24]),
    .in25(Inp32bit[25]), .in26(Inp32bit[26]), .in27(Inp32bit[27]), .in28(Inp32bit[28]), .in29(Inp32bit[29]),
    .in30(Inp32bit[30]), .in31(Inp32bit[31]), .out(Out), .sel(Sel), .en(E));
endmodule
